// Logisim project alu.circ as structural Verilog: 14 circuits, main circuit main
module main (
  input  [31:0] X,
  input  [31:0] Y,
  input  [3:0] Switch,
  output Signed_Overflow,
  output Equal,
  output [31:0] Result
);

  Demultiplexer #(.select(4), .width(32)) demultiplexer_1 (
    .in(X), .sel(Switch));  // open: out0, out1, out2, out3, out4, out5, out6, out7, out8, out9, out10, out11, out12, out13, out14, out15, en
  Demultiplexer #(.select(4), .width(32)) demultiplexer_2 (
    .in(Y), .sel(Switch));  // open: out0, out1, out2, out3, out4, out5, out6, out7, out8, out9, out10, out11, out12, out13, out14, out15, en

  // Other names for the same wires on the sheet: overflow = Signed_Overflow; S[3:0] = Switch

  // Notes on the sheet:
  //   INPUTS to your circuit
  //   DON'T CHANGE THE LOCATIONS OF THE INPUTS AND OUTPUTS!
  //   OUTPUTS from your circuit
endmodule

module sll (
  input  [31:0] B,
  input  [31:0] A,
  output [31:0] out
);

  wire [31:0] multiplexer_1_out, multiplexer_2_out, multiplexer_3_out, multiplexer_4_out, shifter_1_out,
       shifter_2_out, shifter_3_out, shifter_4_out, shifter_5_out;

  Multiplexer #(.width(32)) multiplexer_1 (
    .in0(B), .in1(shifter_1_out), .out(multiplexer_1_out), .sel(A[0]));  // open: en
  Shifter #(.width(32)) shifter_1 (.in(B), .\dist (5'b00001), .out(shifter_1_out));
  Shifter #(.width(32)) shifter_2 (.in(multiplexer_1_out), .\dist (5'b00010), .out(shifter_2_out));
  Multiplexer #(.width(32)) multiplexer_2 (
    .in0(multiplexer_1_out), .in1(shifter_2_out), .out(multiplexer_2_out), .sel(A[1]));  // open: en
  Shifter #(.width(32)) shifter_3 (.in(multiplexer_2_out), .\dist (5'b00100), .out(shifter_3_out));
  Multiplexer #(.width(32)) multiplexer_3 (
    .in0(multiplexer_2_out), .in1(shifter_3_out), .out(multiplexer_3_out), .sel(A[2]));  // open: en
  Shifter #(.width(32)) shifter_4 (.in(multiplexer_3_out), .\dist (5'b01000), .out(shifter_4_out));
  Multiplexer #(.width(32)) multiplexer_4 (
    .in0(multiplexer_3_out), .in1(shifter_4_out), .out(multiplexer_4_out), .sel(A[3]));  // open: en
  Shifter #(.width(32)) shifter_5 (.in(multiplexer_4_out), .\dist (5'b10000), .out(shifter_5_out));
  Multiplexer #(.width(32)) multiplexer_5 (
    .in0(multiplexer_4_out), .in1(shifter_5_out), .out(out), .sel(A[4]));  // open: en
endmodule

module srl (
  input  [31:0] B,
  input  [31:0] A,
  output [31:0] out
);

  wire [31:0] multiplexer_1_out, multiplexer_2_out, multiplexer_3_out, multiplexer_4_out, shifter_1_out,
       shifter_2_out, shifter_3_out, shifter_4_out, shifter_5_out;

  Multiplexer #(.width(32)) multiplexer_1 (
    .in0(B), .in1(shifter_1_out), .out(multiplexer_1_out), .sel(A[0]));  // open: en
  Shifter #(.width(32), .shift("lr")) shifter_1 (.in(B), .\dist (5'b00001), .out(shifter_1_out));
  Shifter #(.width(32), .shift("lr")) shifter_2 (.in(multiplexer_1_out), .\dist (5'b00010), .out(shifter_2_out));
  Multiplexer #(.width(32)) multiplexer_2 (
    .in0(multiplexer_1_out), .in1(shifter_2_out), .out(multiplexer_2_out), .sel(A[1]));  // open: en
  Shifter #(.width(32), .shift("lr")) shifter_3 (.in(multiplexer_2_out), .\dist (5'b00100), .out(shifter_3_out));
  Multiplexer #(.width(32)) multiplexer_3 (
    .in0(multiplexer_2_out), .in1(shifter_3_out), .out(multiplexer_3_out), .sel(A[2]));  // open: en
  Shifter #(.width(32), .shift("lr")) shifter_4 (.in(multiplexer_3_out), .\dist (5'b01000), .out(shifter_4_out));
  Multiplexer #(.width(32)) multiplexer_4 (
    .in0(multiplexer_3_out), .in1(shifter_4_out), .out(multiplexer_4_out), .sel(A[3]));  // open: en
  Shifter #(.width(32), .shift("lr")) shifter_5 (.in(multiplexer_4_out), .\dist (5'b10000), .out(shifter_5_out));
  Multiplexer #(.width(32)) multiplexer_5 (
    .in0(multiplexer_4_out), .in1(shifter_5_out), .out(out), .sel(A[4]));  // open: en
endmodule

module sra (
  input  [31:0] B,
  input  [31:0] A,
  output [31:0] out
);

  wire [31:0] multiplexer_1_out, multiplexer_2_out, multiplexer_3_out, multiplexer_4_out, shifter_1_out,
       shifter_2_out, shifter_3_out, shifter_4_out, shifter_5_out;

  Multiplexer #(.width(32)) multiplexer_1 (
    .in0(B), .in1(shifter_1_out), .out(multiplexer_1_out), .sel(A[0]));  // open: en
  Shifter #(.width(32), .shift("ar")) shifter_1 (.in(B), .\dist (5'b00001), .out(shifter_1_out));
  Shifter #(.width(32), .shift("ar")) shifter_2 (.in(multiplexer_1_out), .\dist (5'b00010), .out(shifter_2_out));
  Multiplexer #(.width(32)) multiplexer_2 (
    .in0(multiplexer_1_out), .in1(shifter_2_out), .out(multiplexer_2_out), .sel(A[1]));  // open: en
  Shifter #(.width(32), .shift("ar")) shifter_3 (.in(multiplexer_2_out), .\dist (5'b00100), .out(shifter_3_out));
  Multiplexer #(.width(32)) multiplexer_3 (
    .in0(multiplexer_2_out), .in1(shifter_3_out), .out(multiplexer_3_out), .sel(A[2]));  // open: en
  Shifter #(.width(32), .shift("ar")) shifter_4 (.in(multiplexer_3_out), .\dist (5'b01000), .out(shifter_4_out));
  Multiplexer #(.width(32)) multiplexer_4 (
    .in0(multiplexer_3_out), .in1(shifter_4_out), .out(multiplexer_4_out), .sel(A[3]));  // open: en
  Shifter #(.width(32), .shift("ar")) shifter_5 (.in(multiplexer_4_out), .\dist (5'b10000), .out(shifter_5_out));
  Multiplexer #(.width(32)) multiplexer_5 (
    .in0(multiplexer_4_out), .in1(shifter_5_out), .out(out), .sel(A[4]));  // open: en
endmodule

module switch (
  input  [31:0] X,
  input  [31:0] Y,
  input  [3:0] Switch,
  output [31:0] out,
  output [31:0] out_2,
  output [31:0] out_3
);

  Demultiplexer #(.select(4), .width(32)) demultiplexer_1 (
    .out0(out), .out2(out_2), .in(X), .sel(Switch));  // open: out1, out3, out4, out5, out6, out7, out8, out9, out10, out11, out12, out13, out14, out15, en
  Demultiplexer #(.select(4), .width(32)) demultiplexer_2 (
    .out0(out_3), .in(Y), .sel(Switch));  // open: out1, out2, out3, out4, out5, out6, out7, out8, out9, out10, out11, out12, out13, out14, out15, en
endmodule

module AND (
  input  [31:0] X,
  input  [31:0] Y,
  output [31:0] Output
);

  assign Output = X & Y;  // AND_Gate and_1, 32 bits wide
endmodule

module OR (
  input  [31:0] X,
  input  [31:0] Y,
  output [31:0] Output
);

  assign Output = X | Y;  // OR_Gate or_1, 32 bits wide
endmodule

module slt__signed_comparison (
  input  [31:0] X,
  input  [31:0] Y,
  output out
);

  Comparator #(.width(32)) comparator_1 (.a(X), .b(Y), .lt(out));  // open: gt, eq
endmodule

module sltu_unsigned_comparison (
  input  [31:0] X,
  input  [31:0] Y,
  output Output
);

  Comparator #(.width(32), .mode("unsigned")) comparator_1 (.a(X), .b(Y), .lt(Output));  // open: gt, eq
endmodule

module Equals (
  input  [31:0] X,
  input  [31:0] Y,
  output Output
);

  Comparator #(.width(32), .mode("unsigned")) comparator_1 (.a(X), .b(Y), .eq(Output));  // open: gt, lt
endmodule

module add (
  input  [31:0] X,
  input  [31:0] Y,
  output [31:0] result,
  output overflow
);

  wire comparator_1_eq, comparator_2_eq, not_1_out;

  Adder #(.width(32)) adder_1 (.a(X), .b(Y), .out(result));  // open: cin, cout
  Comparator #(.width(1), .mode("unsigned")) comparator_1 (.a(X[31]), .b(Y[31]), .eq(comparator_1_eq));  // open: gt, lt
  Comparator #(.width(1), .mode("unsigned")) comparator_2 (
    .a(Y[31]), .b(result[31]), .eq(comparator_2_eq));  // open: gt, lt
  and and_1 (overflow, comparator_1_eq, not_1_out);
  not not_1 (not_1_out, comparator_2_eq);
endmodule

module addu (
  input  [31:0] X,
  input  [31:0] Y,
  output [31:0] result
);

  Adder #(.width(32)) adder_1 (.a(X), .b(Y), .out(result));  // open: cin, cout
endmodule

module sub (
  input  [31:0] in_1,
  input  [31:0] in_2,
  output [31:0] result,
  output overflow
);

  wire and_1_out, and_2_out, and_3_out, and_4_out, comparator_1_gt, comparator_1_lt, multiplexer_1_out,
       multiplexer_2_out, not_1_out, not_2_out, not_3_out;

  Comparator #(.width(1), .mode("unsigned")) comparator_1 (
    .a(in_1[31]), .b(in_2[31]), .gt(comparator_1_gt), .lt(comparator_1_lt));  // open: eq
  not not_1 (not_1_out, comparator_1_gt);
  Subtractor #(.width(32)) subtractor_1 (.a(in_1), .b(in_2), .out(result));  // open: bin, bout
  and and_1 (and_1_out, comparator_1_lt, not_2_out);
  not not_2 (not_2_out, comparator_1_lt);
  and and_2 (and_2_out, comparator_1_gt, not_1_out);
  Multiplexer multiplexer_1 (
    .in0(and_1_out), .in1(comparator_1_lt), .out(multiplexer_1_out), .sel(comparator_1_lt));  // open: en
  Multiplexer multiplexer_2 (
    .in0(and_2_out), .in1(comparator_1_gt), .out(multiplexer_2_out), .sel(comparator_1_gt));  // open: en
  not not_3 (not_3_out, result[31]);
  and and_3 (and_3_out, result[31], multiplexer_1_out);
  and and_4 (and_4_out, not_3_out, multiplexer_2_out);
  or or_1 (overflow, and_3_out, and_4_out);

  // Notes on the sheet:
  //   1; 0
  //   0; 1
endmodule

module subu (
  input  [31:0] in_1,
  input  [31:0] in_2,
  output [31:0] result
);

  Subtractor #(.width(32)) subtractor_1 (.a(in_1), .b(in_2), .out(result));  // open: bin, bout
endmodule
