// Logisim project regfile.circ as structural Verilog: 5 circuits, main circuit main
module main (
  input  [4:0] Read_Register_1,
  input  [4:0] Read_Register_2,
  input  [4:0] Write_Register,
  input  [31:0] Write_Data,
  input  Write_Enable,
  input  Clock,
  output [31:0] s0_Value,
  output [31:0] s1_Value,
  output [31:0] s2_Value,
  output [31:0] ra_Value,
  output [31:0] sp_Value,
  output [31:0] Read_Data_1,
  output [31:0] Read_Data_2
);

  wire [31:0] demultiplexer_1_out1, demultiplexer_1_out2, demultiplexer_1_out3, demultiplexer_1_out4,
       demultiplexer_1_out5, demultiplexer_1_out6, demultiplexer_1_out7, demultiplexer_1_out8,
       demultiplexer_1_out9, demultiplexer_1_out10, demultiplexer_1_out11, demultiplexer_1_out12,
       demultiplexer_1_out13, demultiplexer_1_out14, demultiplexer_1_out15, demultiplexer_1_out16,
       demultiplexer_1_out17, demultiplexer_1_out18, demultiplexer_1_out19, demultiplexer_1_out20,
       demultiplexer_1_out21, demultiplexer_1_out22, demultiplexer_1_out23, demultiplexer_1_out24,
       demultiplexer_1_out25, demultiplexer_1_out26, demultiplexer_1_out27, demultiplexer_1_out28,
       demultiplexer_1_out29, demultiplexer_1_out30, demultiplexer_1_out31;

  registers__0__at__v__a registers_0_at_v_a_1 (
    .sat(demultiplexer_1_out7), .v0(demultiplexer_1_out6), .v1(demultiplexer_1_out5),
    .a0(demultiplexer_1_out4), .a1(demultiplexer_1_out3), .a2(demultiplexer_1_out2),
    .a3(demultiplexer_1_out1), .Write(Write_Enable), .Clock(Clock));  // open: out_0, out_at, out_v0, out_v1, out_a0, out_a1, out_a2, out_a3
  registers__t registers_t_1 (
    .t0(demultiplexer_1_out17), .t1(demultiplexer_1_out16), .t2(demultiplexer_1_out15),
    .t3(demultiplexer_1_out14), .t4(demultiplexer_1_out13), .t5(demultiplexer_1_out12),
    .t6(demultiplexer_1_out11), .t7(demultiplexer_1_out10), .t8(demultiplexer_1_out9),
    .t9(demultiplexer_1_out8), .Write(Write_Enable), .Clock(Clock));  // open: out_t0, out_t1, out_t2, out_t3, out_t4, out_t5, out_t6, out_t7, out_t8, out_t9
  Demultiplexer #(.select(5), .width(32), .enable("false")) demultiplexer_1 (
    .out1(demultiplexer_1_out1), .out2(demultiplexer_1_out2), .out3(demultiplexer_1_out3),
    .out4(demultiplexer_1_out4), .out5(demultiplexer_1_out5), .out6(demultiplexer_1_out6),
    .out7(demultiplexer_1_out7), .out8(demultiplexer_1_out8), .out9(demultiplexer_1_out9),
    .out10(demultiplexer_1_out10), .out11(demultiplexer_1_out11), .out12(demultiplexer_1_out12),
    .out13(demultiplexer_1_out13), .out14(demultiplexer_1_out14), .out15(demultiplexer_1_out15),
    .out16(demultiplexer_1_out16), .out17(demultiplexer_1_out17), .out18(demultiplexer_1_out18),
    .out19(demultiplexer_1_out19), .out20(demultiplexer_1_out20), .out21(demultiplexer_1_out21),
    .out22(demultiplexer_1_out22), .out23(demultiplexer_1_out23), .out24(demultiplexer_1_out24),
    .out25(demultiplexer_1_out25), .out26(demultiplexer_1_out26), .out27(demultiplexer_1_out27),
    .out28(demultiplexer_1_out28), .out29(demultiplexer_1_out29), .out30(demultiplexer_1_out30),
    .out31(demultiplexer_1_out31), .in(Write_Data), .sel(Write_Register));  // open: out0
  registers__s registers_s_1 (
    .s0(demultiplexer_1_out25), .s1(demultiplexer_1_out24), .s2(demultiplexer_1_out23),
    .s3(demultiplexer_1_out22), .s4(demultiplexer_1_out21), .s5(demultiplexer_1_out20),
    .s6(demultiplexer_1_out19), .s7(demultiplexer_1_out18), .out_s0(s0_Value), .out_s1(s1_Value),
    .out_s2(s2_Value), .Write(Write_Enable), .Clock(Clock));  // open: out_s3, out_s4, out_s5, out_s6, out_s7
  registers__k__gp__sp__fp__ra registers_k_gp_sp_fp_ra_1 (
    .k0(demultiplexer_1_out31), .k1(demultiplexer_1_out30), .gp(demultiplexer_1_out29),
    .sp(demultiplexer_1_out28), .fp(demultiplexer_1_out27), .ra(demultiplexer_1_out26), .Write(Write_Enable),
    .out_sp(sp_Value), .out_ra(ra_Value), .Clock(Clock));  // open: out_k0, out_k1, out_gp, out_fp

  // Other names for the same wires on the sheet: clk = Clock; read_data1[31:0] = Read_Data_1;
  //   read_data2[31:0] = Read_Data_2; read_reg1[4:0] = Read_Register_1; read_reg2[4:0] = Read_Register_2;
  //   write_en = Write_Enable; write_reg[4:0] = Write_Register

  // Notes on the sheet:
  //   INPUTS to your circuit
  //   DON'T CHANGE THE LOCATIONS OF THE INPUTS AND OUTPUTS!
  //   These are DEBUG/TEST outputs from your circuit.
  //   OUTPUTS from your circuit
endmodule

module registers__0__at__v__a (
  input  [31:0] sat,
  input  [31:0] v0,
  input  [31:0] v1,
  input  [31:0] a0,
  input  [31:0] a1,
  input  [31:0] a2,
  input  [31:0] a3,
  input  Write,
  input  Clock,
  output [31:0] out_0,
  output [31:0] out_at,
  output [31:0] out_v0,
  output [31:0] out_v1,
  output [31:0] out_a0,
  output [31:0] out_a1,
  output [31:0] out_a2,
  output [31:0] out_a3
);

  Register #(.width(32)) _0 (.Q(out_0), .clk(Clock));  // open: D, en, clr
  Register #(.width(32)) at (.D(sat), .en(Write), .Q(out_at), .clk(Clock));  // open: clr
  Register #(.width(32)) u_v0 (.D(v0), .en(Write), .Q(out_v0), .clk(Clock));  // open: clr
  Register #(.width(32)) u_v1 (.D(v1), .en(Write), .Q(out_v1), .clk(Clock));  // open: clr
  Register #(.width(32)) u_a0 (.D(a0), .Q(out_a0), .clk(Clock));  // open: en, clr
  Register #(.width(32)) u_a1 (.D(a1), .en(Write), .Q(out_a1), .clk(Clock));  // open: clr
  Register #(.width(32)) u_a2 (.D(a2), .en(Write), .Q(out_a2), .clk(Clock));  // open: clr
  Register #(.width(32)) u_a3 (.D(a3), .en(Write), .Q(out_a3), .clk(Clock));  // open: clr
endmodule

module registers__t (
  input  [31:0] t0,
  input  [31:0] t1,
  input  [31:0] t2,
  input  [31:0] t3,
  input  [31:0] t4,
  input  [31:0] t5,
  input  [31:0] t6,
  input  [31:0] t7,
  input  [31:0] t8,
  input  [31:0] t9,
  input  Write,
  input  Clock,
  output [31:0] out_t0,
  output [31:0] out_t1,
  output [31:0] out_t2,
  output [31:0] out_t3,
  output [31:0] out_t4,
  output [31:0] out_t5,
  output [31:0] out_t6,
  output [31:0] out_t7,
  output [31:0] out_t8,
  output [31:0] out_t9
);

  Register #(.width(32)) u_t0 (.D(t0), .en(Write), .Q(out_t0), .clk(Clock));  // open: clr
  Register #(.width(32)) u_t1 (.D(t1), .en(Write), .Q(out_t1), .clk(Clock));  // open: clr
  Register #(.width(32)) u_t2 (.D(t2), .en(Write), .Q(out_t2), .clk(Clock));  // open: clr
  Register #(.width(32)) u_t3 (.D(t3), .en(Write), .Q(out_t3), .clk(Clock));  // open: clr
  Register #(.width(32)) u_t4 (.D(t4), .en(Write), .Q(out_t4), .clk(Clock));  // open: clr
  Register #(.width(32)) u_t5 (.D(t5), .en(Write), .Q(out_t5), .clk(Clock));  // open: clr
  Register #(.width(32)) u_t6 (.D(t6), .en(Write), .Q(out_t6), .clk(Clock));  // open: clr
  Register #(.width(32)) u_t7 (.D(t7), .en(Write), .Q(out_t7), .clk(Clock));  // open: clr
  Register #(.width(32)) u_t8 (.D(t8), .en(Write), .Q(out_t8), .clk(Clock));  // open: clr
  Register #(.width(32)) u_t9 (.D(t9), .en(Write), .Q(out_t9), .clk(Clock));  // open: clr
endmodule

module registers__s (
  input  [31:0] s0,
  input  [31:0] s1,
  input  [31:0] s2,
  input  [31:0] s3,
  input  [31:0] s4,
  input  [31:0] s5,
  input  [31:0] s6,
  input  [31:0] s7,
  input  Write,
  input  Clock,
  output [31:0] out_s0,
  output [31:0] out_s1,
  output [31:0] out_s2,
  output [31:0] out_s3,
  output [31:0] out_s4,
  output [31:0] out_s5,
  output [31:0] out_s6,
  output [31:0] out_s7
);

  Register #(.width(32)) u_s0 (.D(s0), .en(Write), .Q(out_s0), .clk(Clock));  // open: clr
  Register #(.width(32)) u_s1 (.D(s1), .en(Write), .Q(out_s1), .clk(Clock));  // open: clr
  Register #(.width(32)) u_s2 (.D(s2), .en(Write), .Q(out_s2), .clk(Clock));  // open: clr
  Register #(.width(32)) u_s3 (.D(s3), .en(Write), .Q(out_s3), .clk(Clock));  // open: clr
  Register #(.width(32)) u_s4 (.D(s4), .en(Write), .Q(out_s4), .clk(Clock));  // open: clr
  Register #(.width(32)) u_s5 (.D(s5), .en(Write), .Q(out_s5), .clk(Clock));  // open: clr
  Register #(.width(32)) u_s6 (.D(s6), .en(Write), .Q(out_s6), .clk(Clock));  // open: clr
  Register #(.width(32)) u_s7 (.D(s7), .en(Write), .Q(out_s7), .clk(Clock));  // open: clr
endmodule

module registers__k__gp__sp__fp__ra (
  input  [31:0] k0,
  input  [31:0] k1,
  input  [31:0] gp,
  input  [31:0] sp,
  input  [31:0] fp,
  input  [31:0] ra,
  input  Write,
  input  Clock,
  output [31:0] out_k0,
  output [31:0] out_k1,
  output [31:0] out_gp,
  output [31:0] out_sp,
  output [31:0] out_fp,
  output [31:0] out_ra
);

  Register #(.width(32)) u_k0 (.D(k0), .en(Write), .Q(out_k0), .clk(Clock));  // open: clr
  Register #(.width(32)) u_k1 (.D(k1), .en(Write), .Q(out_k1), .clk(Clock));  // open: clr
  Register #(.width(32)) u_gp (.D(gp), .en(Write), .Q(out_gp), .clk(Clock));  // open: clr
  Register #(.width(32)) u_sp (.D(sp), .en(Write), .Q(out_sp), .clk(Clock));  // open: clr
  Register #(.width(32)) u_fp (.D(fp), .en(Write), .Q(out_fp), .clk(Clock));  // open: clr
  Register #(.width(32)) u_ra (.D(ra), .en(Write), .Q(out_ra), .clk(Clock));  // open: clr
endmodule
